# Fritzing sketch 7-5 (saved by Fritzing 0.9.4)
breadboards: 1

parts:
  J1 = female pin header, 8 pins [form="♀ (female)"]
  Keypad4x1 = Keypad Membran 4x4
  Part1 = Arduino Uno (Rev3)
  LED1 = LED - 5mm [color="Red (633nm)" package="5 mm [THT]"]
  R1 = Resistor [tolerance=±5% resistance=220 package=THT]

nets:
  N1: J1.pin1, Keypad4x1.Pin1, Part1.D9_PWM
  N2: J1.pin2, Keypad4x1.Pin2, Part1.D8
  N3: J1.pin3, Keypad4x1.Pin3, Part1.D7
  N4: J1.pin4, Keypad4x1.Pin4, Part1.D6_PWM
  N5: J1.pin5, Keypad4x1.Pin5, Part1.D5_PWM
  N6: J1.pin6, Keypad4x1.Pin6, Part1.D4
  N7: J1.pin7, Keypad4x1.Pin7, Part1.D3_PWM
  N8: J1.pin8, Keypad4x1.Pin8, Part1.D2
  N9: Part1.D13/SCK, LED1.cathode
  N10: Part1.GND, R1.Pin_1
  N11: LED1.anode, R1.Pin_0

custom parts:
  Keypad Membran 4x4: Membrane Keypad 4x4 Matrix
